// Logisim project Ula-32BITS.circ as structural Verilog: 1 circuit, main circuit main
module main (
  input  [2:0] in_1,
  input  bInvert,
  input  [31:0] in_3,
  input  [31:0] in_4,
  output out_5,
  output Overflow
);

  wire main_1_p3, main_1_p5, main_1_p8, main_2_p5, main_2_p8, main_3_p5, main_3_p8, main_4_p5, main_4_p8,
       main_5_p5, main_5_p8, main_6_p5, main_6_p8, main_7_p5, main_7_p8, main_8_p5, main_8_p8, main_9_p5,
       main_9_p8, main_10_p5, main_10_p8, main_11_p5, main_11_p8, main_12_p5, main_12_p8, main_13_p5,
       main_13_p8, main_14_p5, main_14_p8, main_15_p5, main_15_p8, main_16_p5, main_16_p8, main_17_p5,
       main_17_p8, main_18_p5, main_18_p8, main_19_p5, main_19_p8, main_20_p5, main_20_p8, main_21_p5,
       main_21_p8, main_22_p5, main_22_p8, main_23_p5, main_23_p8, main_24_p5, main_24_p8, main_25_p5,
       main_25_p8, main_26_p5, main_26_p8, main_27_p5, main_27_p8, main_28_p5, main_28_p8, main_29_p5,
       main_29_p8, main_30_p5, main_30_p8, main_31_p5, main_31_p8, main_32_p8, or_1_out;

  // Ula_1bit_main main_1: pin names not known; wires that end beside it: in_3[0], in_4[0], main_1_p3, bInvert, main_1_p5, bInvert, in_1[1], main_1_p8
  // Ula_1bit_main main_2: pin names not known; wires that end beside it: in_3[1], in_4[1], 1'b0, bInvert, main_2_p5, main_1_p5, in_1[1], main_2_p8
  // Ula_1bit_main main_3: pin names not known; wires that end beside it: in_3[2], in_4[2], 1'b0, bInvert, main_3_p5, main_2_p5, in_1[1], main_3_p8
  // Ula_1bit_main main_4: pin names not known; wires that end beside it: in_3[3], in_4[3], 1'b0, bInvert, main_4_p5, main_3_p5, in_1[1], main_4_p8
  // Ula_1bit_main main_5: pin names not known; wires that end beside it: in_3[4], in_4[4], 1'b0, bInvert, main_5_p5, main_4_p5, in_1[1], main_5_p8
  // Ula_1bit_main main_6: pin names not known; wires that end beside it: in_3[5], in_4[5], 1'b0, bInvert, main_6_p5, main_5_p5, in_1[1], main_6_p8
  // Ula_1bit_main main_7: pin names not known; wires that end beside it: in_3[6], in_4[6], 1'b0, bInvert, main_7_p5, main_6_p5, in_1[1], main_7_p8
  // Ula_1bit_main main_8: pin names not known; wires that end beside it: in_3[7], in_4[7], 1'b0, bInvert, main_8_p5, main_7_p5, in_1[1], main_8_p8
  // Ula_1bit_main main_9: pin names not known; wires that end beside it: in_3[8], in_4[8], 1'b0, bInvert, main_9_p5, main_8_p5, in_1[1], main_9_p8
  // Ula_1bit_main main_10: pin names not known; wires that end beside it: in_3[9], in_4[9], 1'b0, bInvert, main_10_p5, main_9_p5, in_1[1], main_10_p8
  // Ula_1bit_main main_11: pin names not known; wires that end beside it: in_3[10], in_4[10], 1'b0, bInvert, main_11_p5, main_10_p5, in_1[1], main_11_p8
  // Ula_1bit_main main_12: pin names not known; wires that end beside it: in_3[11], in_4[11], 1'b0, bInvert, main_12_p5, main_11_p5, in_1[1], main_12_p8
  // Ula_1bit_main main_13: pin names not known; wires that end beside it: in_3[12], in_4[12], 1'b0, bInvert, main_13_p5, main_12_p5, in_1[1], main_13_p8
  // Ula_1bit_main main_14: pin names not known; wires that end beside it: in_3[13], in_4[13], 1'b0, bInvert, main_14_p5, main_13_p5, in_1[1], main_14_p8
  // Ula_1bit_main main_15: pin names not known; wires that end beside it: in_3[14], in_4[14], 1'b0, bInvert, main_15_p5, main_14_p5, in_1[1], main_15_p8
  // Ula_1bit_main main_16: pin names not known; wires that end beside it: in_3[15], in_4[15], 1'b0, bInvert, main_16_p5, main_15_p5, in_1[1], main_16_p8
  // Ula_1bit_main main_17: pin names not known; wires that end beside it: in_3[16], in_4[16], 1'b0, bInvert, main_17_p5, main_16_p5, in_1[1], main_17_p8
  // Ula_1bit_main main_18: pin names not known; wires that end beside it: in_3[17], in_4[17], 1'b0, bInvert, main_18_p5, main_17_p5, in_1[1], main_18_p8
  // Ula_1bit_main main_19: pin names not known; wires that end beside it: in_3[18], in_4[18], 1'b0, bInvert, main_19_p5, main_18_p5, in_1[1], main_19_p8
  // Ula_1bit_main main_20: pin names not known; wires that end beside it: in_3[19], in_4[19], 1'b0, bInvert, main_20_p5, main_19_p5, in_1[1], main_20_p8
  // Ula_1bit_main main_21: pin names not known; wires that end beside it: in_3[20], in_4[20], 1'b0, bInvert, main_21_p5, main_20_p5, in_1[1], main_21_p8
  // Ula_1bit_main main_22: pin names not known; wires that end beside it: in_3[21], in_4[21], 1'b0, bInvert, main_22_p5, main_21_p5, in_1[1], main_22_p8
  // Ula_1bit_main main_23: pin names not known; wires that end beside it: in_3[22], in_4[22], 1'b0, bInvert, main_23_p5, main_22_p5, in_1[1], main_23_p8
  // Ula_1bit_main main_24: pin names not known; wires that end beside it: in_3[23], in_4[23], 1'b0, bInvert, main_24_p5, main_23_p5, in_1[1], main_24_p8
  // Ula_1bit_main main_25: pin names not known; wires that end beside it: in_3[24], in_4[24], 1'b0, bInvert, main_25_p5, main_24_p5, in_1[1], main_25_p8
  // Ula_1bit_main main_26: pin names not known; wires that end beside it: in_3[25], in_4[25], 1'b0, bInvert, main_26_p5, main_25_p5, in_1[1], main_26_p8
  // Ula_1bit_main main_27: pin names not known; wires that end beside it: in_3[26], in_4[26], 1'b0, bInvert, main_27_p5, main_26_p5, in_1[1], main_27_p8
  // Ula_1bit_main main_28: pin names not known; wires that end beside it: in_3[27], in_4[27], 1'b0, bInvert, main_28_p5, main_27_p5, in_1[1], main_28_p8
  // Ula_1bit_main main_29: pin names not known; wires that end beside it: in_3[28], in_4[28], 1'b0, bInvert, main_29_p5, main_28_p5, in_1[1], main_29_p8
  // Ula_1bit_main main_30: pin names not known; wires that end beside it: in_3[29], in_4[29], 1'b0, bInvert, main_30_p5, main_29_p5, in_1[1], main_30_p8
  // Ula_1bit_main main_31: pin names not known; wires that end beside it: in_3[30], in_4[30], 1'b0, bInvert, main_31_p5, main_30_p5, in_1[1], main_31_p8
  // Ula_32bit_main main_32: pin names not known; wires that end beside it: in_3[31], in_4[31], 1'b0, bInvert, Overflow, main_31_p5, in_1[1], main_32_p8, main_1_p3
  or or_1 (or_1_out, main_1_p8, main_2_p8, main_3_p8, main_4_p8, main_5_p8, main_6_p8, main_7_p8, main_8_p8, main_9_p8, main_10_p8, main_11_p8, main_12_p8, main_13_p8, main_14_p8, main_15_p8, main_16_p8, main_17_p8, main_18_p8, main_19_p8, main_20_p8, main_21_p8, main_22_p8, main_23_p8, main_24_p8, main_25_p8, main_26_p8, main_27_p8, main_28_p8, main_29_p8, main_30_p8, main_31_p8, main_32_p8);
  not not_1 (out_5, or_1_out);
  // Pins of 1 and 3 bits meet at {bInvert, {2{in_1[1]}}}

  assign {in_1[2], in_1[0]} = {bInvert, in_1[1]};
endmodule
